// Digital circuit CPU.dig as structural Verilog
module CPU (
  input  CLK,
  input  RegF_WE,
  input  [3:0] BranchLine,
  input  GoBranch,
  input  in_13,
  input  in_14,
  input  in_15,
  input  in_16,
  input  in_17,
  input  in_18,
  input  in_19,
  input  in_20,
  output out_5,
  output out_6,
  output out_7,
  output out_8,
  output out_9,
  output out_10,
  output out_11,
  output out_12
);

  wire counterpreset_1_ovf, ID_IMM_check, rom_1_d, rom_2_d, undriven;
  wire [1:0] EX_Do_SMTH;
  wire [2:0] EX_Do_Math, EX_R_Dest, EX_SMTH_Choice, ID_R_Dest, ID_R_Src1;
  wire [3:0] ALU_c_f, EX_Reg_F, ID_Opcode, PC_Out;
  wire [7:0] EX_ALU_output, EX_Data_A, EX_Data_B, EX_DataA, EX_DataB, ID_Data_A, ID_Data_B, ID_R_Src2_IMM,
       R_Src_2_Out;
  wire [18:0] Instruction_d;
  wire [22:0] rom_3_d;
  wire [23:23] undriven_2;

  CounterPreset #(.Bits(4)) counterpreset_1 (
    .en(1'b1), .C(CLK), .dir(1'b0), .in(BranchLine), .ld(GoBranch), .clr(counterpreset_1_ovf), .out(PC_Out),
    .ovf(counterpreset_1_ovf));
  RAMDualPort ramdualport_1 ();  // open: A, Din, str, C, ld, D
  ROM #(.AddrBits(4), .Bits(19)) Instruction (.A(PC_Out), .sel(1'b1), .D(Instruction_d));
  ROM rom_1 (.A(EX_Do_SMTH), .sel(1'b1), .D(rom_1_d));
  ROM rom_2 (.A(EX_SMTH_Choice[1:0]), .sel(1'b1), .D(rom_2_d));
  Register #(.Bits(19)) IF_ID (
    .D(Instruction_d), .C(CLK), .en(1'b1), .Q({ID_IMM_check, ID_Opcode, ID_R_Dest, ID_R_Src1, ID_R_Src2_IMM}));
  Register ME_WB (.C(CLK), .en(1'b1));  // open: D, Q
  ALU ALU (
    .A(EX_DataA), .B(EX_DataB), .Do_Math(EX_Do_Math), .Res(EX_ALU_output), .C_F(ALU_c_f[0]),
    .O_F(ALU_c_f[1]), .N_F(ALU_c_f[2]), .Z_F(ALU_c_f[3]));
  RegisterFile #(.AddrBits(3), .Bits(8)) RegFile (
    .Din(EX_ALU_output), .we(RegF_WE), .Rw(ID_R_Dest), .C(CLK), .Ra(ID_R_Src1), .Rb(ID_R_Src2_IMM[2:0]),
    .Da(ID_Data_A), .Db(R_Src_2_Out));
  ROM #(.AddrBits(4), .Bits(23)) rom_3 (.A(ID_Opcode), .sel(1'b1), .D(rom_3_d));
  Multiplexer #(.Bits(8)) multiplexer_1 (.sel(ID_IMM_check), .in_0(R_Src_2_Out), .in_1(ID_R_Src2_IMM), .out(ID_Data_B));
  flag_register flag_register_1 (.CONZ_i(ALU_c_f), .Do_Write(undriven), .CONZ_o(EX_Reg_F));
  Register #(.Bits(24)) ID_EX (
    .D({undriven_2[23], rom_3_d[3:0], ID_R_Dest, ID_Data_A, ID_Data_B}), .C(CLK), .en(1'b1),
    .Q({EX_Do_SMTH, EX_SMTH_Choice, EX_R_Dest, EX_Data_A, EX_Data_B}));
  Register EX_ME (.C(CLK), .en(1'b1));  // open: D, Q
  // Pins of 4 and 23 bits meet at rom_3_d
  // Pins of 2 and 3 bits meet at EX_SMTH_Choice

  // Other names for the same wires on the sheet: Go_Branch = GoBranch;
  //   ID_EX[23:0] = {EX_Do_SMTH, EX_SMTH_Choice, EX_R_Dest, EX_Data_A, EX_Data_B}; Line_Branch[3:0] = BranchLine

  // Notes on the sheet:
  //   RegF_WE: default 1
  //   Pipeline Stages
  //   Instruction Fetch
  //   Execute
  //   Memory
  //   Opcode
  //   0000: LD
  //   0001: MOV
  //   0010: ST
  //   0011: RD
  //   0100: ADD
  //   0101L SUB
  //   0110: MUL
  //   0111: WR
  //   1000: AND
  //   1001: OR
  //   1010: XOR
  //   1011: NOT
  //   1100: BC
  //   1101:BZ
  //   1110: BNZ
  //   1111:B
  //   Do_{GPIO}
  //   Do_{Mem}
  //   contents of Instruction (hex, n*v repeats v):
  //   40a0f,4103f,5a01
  //   Do_{Math}
  //   Do_{Jump}
  //   Instruction Decode
  //   CU
  //   Do_{SMTH}: 4:3
  //   00 Do_{Math}
  //   01 Do_{GPIO}
  //   10 Do_{Jump} (IMM only)
  //   11 Do_{Mem} (IMM only)
  //   SMTH_{Choice}: 2:0
  //   contents of rom_3 (hex, n*v repeats v):
  //   4,5
  //   Write Back
endmodule
